# Fritzing sketch PreventCataclysmSystems (saved by Fritzing 0.9.3b)
breadboards: 1

parts:
  Raspberry_Pi1 = Raspberry Pi 2
  DHT1 = DHT11 Humitidy and Temperature Sensor
  R1 = Resistor [tolerance=±5% resistance=2.2 package="0603 [SMD]"]

nets:
  3V3: Raspberry_Pi1.3v3, DHT1.VDD, R1.Pin_0
  N1: Raspberry_Pi1.GPIO4, DHT1.DATA, R1.Pin_1
  GND: Raspberry_Pi1.GND, DHT1.GND

custom parts:
  DHT11 Humitidy and Temperature Sensor: DHT11 Humidity and Temperature Sensor
